# Fritzing sketch BVS (saved by Fritzing 0.9.3b)

parts:
  Mod1 = sensor_biometrico
  U1 = NodeMCU V1.0
  LED1 = LEDs [package=led10mm]
  LED2 = LEDs [package=led10mm]

nets:
  VCC: Mod1.VCC, U1.3V3
  N1: Mod1.TX, U1.D2
  N2: Mod1.RX, U1.D3
  GND: Mod1.GND, U1.GND, LED2.A
  N3: U1.D6, LED1.C
  N4: U1.D7, LED2.C

custom parts:
  sensor_biometrico: Adafruit Optical Fingerprint Sensor
  NodeMCU V1.0: ESP8266 based NodeMCU
